# Fritzing sketch arduino_water_level_indicator (saved by Fritzing 0.9.2b)
breadboards: 1

parts:
  IC1 = MICROCONTROLLER [part_number=ATMega328P package=dil28-3-zif_socket]
  L7805 = Voltage Regulator - 5V [package="DPak [SMD]"]
  C1 = Capacitor [part_number=22pf package=cap-pth-small2]
  C2 = Capacitor [part_number=22pf package=cap-pth-small2]
  VCC1 = Battery block 9V
  U1 = SWITCH_SPDT [part_number=Switch package=kps-1290]
  16Mhz = CRYSTAL [package=hc49us]
  R1 = Resistor [tolerance=±5% resistance=10k package="2512 [SMD]"]
  C3 = Electrolytic Capacitor [capacitance=10µF package="0405 [SMD, electrolytic]"]
  C4 = Electrolytic Capacitor [capacitance=10µF package="0405 [SMD, electrolytic]"]
  Part1 = SRF05 Ultrasonic Rangefinder
  C5 = Electrolytic Capacitor [capacitance=10µF package="100 mil [THT, electrolytic]"]
  D1 = LED_BARGRAPH_10 [package=led_bargaph_10]

nets:
  N1: IC1.PC6(_RESET), R1.Pin_0
  N2: IC1.VCC, L7805.output_voltage, R1.Pin_1
  GND: IC1.GND, IC1.AGND, L7805.GND, C1.2, C2.1, VCC1.-, C3.-, C4.-, Part1.GND, C5.-, D1.J_C, D1.I_C, D1.H_C, D1.G_C, D1.F_C, D1.E_C, D1.D_C, D1.C_C, D1.B_C, D1.A_C
  N3: IC1.PB6(XTAL1_TOSC1), C2.2, 16Mhz.1
  N4: IC1.PB7(XTAL2_TOSC2), C1.1, 16Mhz.2
  N5: L7805.input_voltage, U1.P, C3.+
  N6: VCC1.+, U1.O
  N7: C4.+, Part1.VCC, C5.+

notes:
  To Pin 19
  To Pin 13
  To Pin 11
  To Pin 12
  To Pin 14
  To Pin 18
  To Pin 17
  To Pin 16
  To Pin 15
  To Pin 6
  To Pin 5
  To Pin 4
  Arduino Water Level Indicator MK-II
  Ping Sensor
  LED Bar Graph Display
  (Can be replaced by regular LEDs)
  Note:-
  The pin nos. specified in this diagram correspond to the pins of the microcontroller and NOT that of the Arduino
